// Digital circuit 09-icpu-ir.dig as structural Verilog
module _09_icpu_ir (
  input  CLOCK,
  input  RO,
  input  MI,
  input  CO,
  input  CE,
  input  CODEI,
  input  RANDI,
  input  RANDO,
  input  JMP,
  input  BIE,
  input  BOE,
  input  AIE,
  input  AOE,
  input  RST,
  input  IO,
  input  RW,
  input  _0,
  input  _1,
  input  _2,
  input  _3,
  input  _4,
  input  _5,
  input  _6,
  input  _7,
  input  in_25,
  input  in_26
);

  wire AIE_t, AOE_t, BIE_t, BOE_t, ERR, IN_IOE, IRCI, IRO, IRRI, JMP_t, nor_1_out, PCOE, RAIE, ROE, RST_t,
       RWE;
  wire [3:0] _02_register_1_p2, _02_register_1_p8;
  wire [7:0] _02_register_1_p11, DEBUG_IROPCODE, RAM_d;

  // _02_register _02_register_1: pin names not known; wires that end beside it: _02_register_1_p2[0], _02_register_1_p2[1], _02_register_1_p2[2], _02_register_1_p2[3], _02_register_1_p8[0], _02_register_1_p8[1], _02_register_1_p8[2], _02_register_1_p8[3], RAIE, CLOCK, _02_register_1_p11[0], _02_register_1_p11[1], _02_register_1_p11[2], _02_register_1_p11[3], _02_register_1_p11[4], _02_register_1_p11[5], _02_register_1_p11[6], _02_register_1_p11[7], 1'b0, RST
  // _02_register _02_register_2: pin names not known; wires that end beside it: DEBUG_IROPCODE[7], DEBUG_IROPCODE[7], _02_register_1_p8[3], DEBUG_IROPCODE[6], DEBUG_IROPCODE[6], _02_register_1_p8[2], DEBUG_IROPCODE[5], DEBUG_IROPCODE[5], _02_register_1_p8[1], DEBUG_IROPCODE[4], DEBUG_IROPCODE[4], _02_register_1_p8[0], DEBUG_IROPCODE[3], DEBUG_IROPCODE[3], _02_register_1_p2[3], DEBUG_IROPCODE[2], DEBUG_IROPCODE[2], _02_register_1_p2[2]
  // _02_register _02_register_3: pin names not known; wires that end beside it: DEBUG_IROPCODE[1], DEBUG_IROPCODE[1], _02_register_1_p2[1], DEBUG_IROPCODE[0], DEBUG_IROPCODE[0], _02_register_1_p2[0], 1'b0, IRCI, RST, CLOCK, _02_register_1_p8[3], _02_register_1_p8[3], _02_register_1_p8[2], _02_register_1_p8[2], _02_register_1_p8[1], _02_register_1_p8[1], _02_register_1_p8[0], _02_register_1_p8[0], _02_register_1_p2[3], _02_register_1_p2[3], _02_register_1_p2[2], _02_register_1_p2[2], _02_register_1_p2[1], _02_register_1_p2[1], _02_register_1_p2[0], _02_register_1_p2[0], IRO, IRRI, RST, CLOCK
  RAMSinglePortSel #(.AddrBits(8), .Bits(8)) RAM (.A(_02_register_1_p11), .CS(~1'b0), .WE(~RWE), .OE(~ROE), .D(RAM_d));
  nor nor_1 (nor_1_out, 1'b0, ~RWE, ROE);  // NOr
  not not_1 (IN_IOE, IO);
  not not_2 (RWE, RW);
  not not_3 (RAIE, MI);
  // _02_register _02_register_4: pin names not known; wires that end beside it: CLOCK, RST, AIE_t, AOE_t, _02_register_1_p8[3], _02_register_1_p8[3], _02_register_1_p8[2], _02_register_1_p8[2], _02_register_1_p8[1], _02_register_1_p8[1], _02_register_1_p8[0], _02_register_1_p8[0], _02_register_1_p2[3], _02_register_1_p2[3], _02_register_1_p2[2], _02_register_1_p2[2], _02_register_1_p2[1], _02_register_1_p2[1], _02_register_1_p2[0], _02_register_1_p2[0]
  BusSplitter #(.Bits(8)) bussplitter_1 (
    .D(RAM_d), .OE(nor_1_out), .D0(_02_register_1_p2[0]), .D1(_02_register_1_p2[1]),
    .D2(_02_register_1_p2[2]), .D3(_02_register_1_p2[3]), .D4(_02_register_1_p8[0]),
    .D5(_02_register_1_p8[1]), .D6(_02_register_1_p8[2]), .D7(_02_register_1_p8[3]));
  not not_4 (ROE, RO);
  not not_5 (PCOE, CO);
  LED u__7 (.in(_02_register_1_p8[3]));
  not not_6 (JMP_t, JMP);
  LED u__6 (.in(_02_register_1_p8[2]));
  LED u__5 (.in(_02_register_1_p8[1]));
  not not_7 (IRCI, CODEI);
  not not_8 (IRRI, RANDI);
  LED u__4 (.in(_02_register_1_p8[0]));
  LED u__3 (.in(_02_register_1_p2[3]));
  not not_9 (IRO, RANDO);
  LED u__2 (.in(_02_register_1_p2[2]));
  LED u__1 (.in(_02_register_1_p2[1]));
  not not_10 (BIE_t, BIE);
  LED u__0 (.in(_02_register_1_p2[0]));
  not not_11 (AIE_t, AIE);
  not not_12 (BOE_t, BOE);
  Seven_Seg_Hex seven_seg_hex_1 (.d(_02_register_1_p8), .dp(1'b0));
  not not_13 (AOE_t, AOE);
  Seven_Seg_Hex seven_seg_hex_2 (.d(_02_register_1_p2), .dp(1'b0));
  _74245 _74245_1 (
    .pin1(1'b1), .pin2(_7), .pin3(_6), .pin4(_5), .pin5(_4), .pin6(_3), .pin7(_2), .pin8(_1), .pin9(_0),
    .pin10(1'b0), .pin11(_02_register_1_p2[0]), .pin12(_02_register_1_p2[1]), .pin13(_02_register_1_p2[2]),
    .pin14(_02_register_1_p2[3]), .pin15(_02_register_1_p8[0]), .pin16(_02_register_1_p8[1]),
    .pin17(_02_register_1_p8[2]), .pin18(_02_register_1_p8[3]), .pin19(IN_IOE), .pin20(1'b1));
  // _02_register _02_register_5: pin names not known; wires that end beside it: _02_register_1_p2[0], _02_register_1_p2[0], _02_register_1_p2[1], _02_register_1_p2[1], _02_register_1_p2[2], _02_register_1_p2[2], _02_register_1_p2[3], _02_register_1_p2[3], _02_register_1_p8[0], _02_register_1_p8[0], _02_register_1_p8[1], _02_register_1_p8[1], _02_register_1_p8[2], _02_register_1_p8[2], _02_register_1_p8[3], _02_register_1_p8[3], BOE_t, BIE_t, RST, CLOCK
  _07_program_counter _07_program_counter_1 (
    .D0(_02_register_1_p2[0]), .D1(_02_register_1_p2[1]), .D2(_02_register_1_p2[2]),
    .D3(_02_register_1_p2[3]), .D4(_02_register_1_p8[0]), .D5(_02_register_1_p8[1]),
    .D6(_02_register_1_p8[2]), .D7(_02_register_1_p8[3]), .Q1(_02_register_1_p2[1]),
    .Q2(_02_register_1_p2[2]), .Q3(_02_register_1_p2[3]), .Q0(_02_register_1_p2[0]),
    .Q5(_02_register_1_p8[1]), .Q6(_02_register_1_p8[2]), .Q7(_02_register_1_p8[3]),
    .Q4(_02_register_1_p8[0]), .RST(RST_t), .JMP(JMP_t), .PCCE(CE), .ERR(ERR), .CLK(CLOCK), .PCOE(PCOE));
  not not_14 (RST_t, RST);
  LED led_1 (.in(ERR));
  Seven_Seg_Hex seven_seg_hex_3 (.d(DEBUG_IROPCODE[3:0]), .dp(1'b0));
  Seven_Seg_Hex seven_seg_hex_4 (.d(DEBUG_IROPCODE[7:4]), .dp(1'b0));

  // Other names for the same wires on the sheet: CLK = CLOCK; PCCE = CE

  // Notes on the sheet:
  //   Register A
  //   Register B
endmodule
